# Fritzing sketch OZ_FIRE (saved by Fritzing 0.9.3b)

parts:
  Part1 = Arduino Uno (Rev3)
  Q1 = Basic FET N-Channel [package="DPak [SMD]"]
  C1 = Capacitor Polarized [package=nippon_f80]
  M1 = DC Motor
  NEOPIXEL1 = Neopixel Strip -- White (60/m)
  D1 = Rectifier Diode [part_number=1N4001 package="300 mil [THT]"]
  D2 = Rectifier Diode [part_number=1N4001 package="300 mil [THT]"]
  D3 = Rectifier Diode [part_number=1N4001 package="300 mil [THT]"]
  D4 = Rectifier Diode [part_number=1N4001 package="300 mil [THT]"]
  IC1 = Voltage Regulator [package=to-220-alt]
  VCC1 = Battery block 9V
  S1 = Square Pushbutton
  R1 = Resistor [tolerance=±5% resistance=10k package=THT]

nets:
  N1: Part1.D11_PWM/MOSI, Q1.Gate
  GND: Part1.GND, Q1.source, NEOPIXEL1.GND, D2.cathode, D3.cathode, IC1.GND, R1.Pin_0
  N2: Part1.D1/TX, S1.leg1, R1.Pin_1
  N3: Part1.D6_PWM, NEOPIXEL1.DI
  5V: Part1.5V, NEOPIXEL1.+5V, S1.leg0
  N4: Part1.VIN, C1.+, M1.pin_2, IC1.OUT
  N5: Q1.drain, C1.-, M1.pin_1
  N6: D1.cathode, D2.anode, VCC1.+
  N7: D1.anode, D4.anode, IC1.IN
  N8: D3.anode, D4.cathode, VCC1.-

custom parts:
  Neopixel Strip -- White (60/m): Neopixel Strip, White, 60 pixels per meter.
